// Digital circuit RV32I-Control.dig as structural Verilog
module RV32I_Control (
  input  Start,
  input  Pause,
  input  Reset,
  input  Hold,
  input  Error,
  input  CLC,
  input  Boot_Complete,
  input  Boot_Counter_Overflow,
  output Normal,
  output Run,
  output Go,
  output Error_2,
  output Boot_Counter_Enable,
  output Boot_Counter_Set_Memory_R_W_Address,
  output ROM_Set_Memory_R_W
);

  D_FF Boot_Normal (.C(CLC), .Q(Normal));  // open: D, nQ
  D_FF Pause_Run (.C(CLC), .Q(Run));  // open: D, nQ

  // Notes on the sheet:
  //   STATUS
endmodule
