// Digital circuit RV32I-Decode-Control.dig as structural Verilog
module RV32I_Decode_Control (
  input  [31:0] INSTR,
  input  Normal,
  input  Run,
  input  Go,
  output DECODE_HOLD,
  output DECODE_EN,
  output RESERVE,
  output ERROR
);

  wire rv32i_decode_instruction_decoder_1_e, rv32i_decode_instruction_decoder_1_reg_hold;

  RV32I_Decode_Instruction_Decoder rv32i_decode_instruction_decoder_1 (
    .IN(INSTR), .REG_HOLD(rv32i_decode_instruction_decoder_1_reg_hold),
    .E(rv32i_decode_instruction_decoder_1_e));
  and and_1 (DECODE_HOLD, ~INSTR[4], INSTR[5], INSTR[6]);  // And
  and and_2 (DECODE_EN, Normal, Run);
  and and_3 (RESERVE, rv32i_decode_instruction_decoder_1_reg_hold, Normal, Run);
  and and_4 (ERROR, rv32i_decode_instruction_decoder_1_e, Run, Normal, Go);
endmodule
