// Digital circuit RV32I-Execute-Control.dig as structural Verilog
module RV32I_Execute_Control (
  input  [31:0] INSTR,
  input  Normal,
  input  Run,
  input  Go,
  output EXECUTE_HOLD,
  output EXECUTE_EN,
  output ALU_SET_REGISTER,
  output ALU_SET_PC,
  output ALU_SET_MEMORY_A,
  output [7:0] ALU_INSTR,
  output [4:0] RS1_A,
  output [4:0] RS2_A
);

  wire [2:2] rv32i_instruction_decoder_1_p3;

  // RV32I_Instruction_Decoder rv32i_instruction_decoder_1: pin names not known; wires that end beside it: INSTR, EXECUTE_HOLD, {rv32i_instruction_decoder_1_p3[2], ALU_SET_PC, ALU_SET_REGISTER}, ALU_INSTR
  and and_1 (EXECUTE_EN, Normal, Run);
  and and_2 (ALU_SET_MEMORY_A, rv32i_instruction_decoder_1_p3[2], Normal);
  PullDown pulldown_1 ();  // open: out

  assign RS1_A = INSTR[19:15];
  assign RS2_A = INSTR[24:20];

  // Notes on the sheet:
  //   ALU_SET_PC: A
endmodule
