// Digital circuit RV32I-Fetch-Control.dig as structural Verilog
module RV32I_Fetch_Control (
  input  Normal,
  input  Run,
  input  Go,
  input  JUMP,
  output PC_EN,
  output PC_INC_SET_PC,
  output PC_STALL
);

  and and_1 (PC_EN, Normal, Run);
  and and_2 (PC_INC_SET_PC, Go, ~JUMP);  // And
  and and_3 (PC_STALL, ~Go, ~JUMP);  // And
endmodule
