// Digital circuit RV32I-Instruction-Decoder.dig as structural Verilog
module RV32I_Instruction_Decoder (
  input  [31:0] IN,
  output [36:0] I,
  output R
);

  and and_1 (I[0], IN[29], IN[1], ~IN[2], ~IN[3], IN[4], IN[5], ~IN[6], ~IN[12], ~IN[13], ~IN[14], ~IN[25], ~IN[26], ~IN[27], ~IN[28], ~IN[29], ~IN[30], ~IN[31]);  // And
  and and_2 (I[1], IN[29], IN[1], ~IN[2], ~IN[3], IN[4], IN[5], ~IN[6], ~IN[12], ~IN[13], ~IN[14], ~IN[25], ~IN[26], ~IN[27], ~IN[28], ~IN[29], IN[30], ~IN[31]);  // And
  and and_3 (I[2], IN[29], IN[1], ~IN[2], ~IN[3], IN[4], IN[5], ~IN[6], IN[12], IN[13], IN[14], ~IN[25], ~IN[26], ~IN[27], ~IN[28], ~IN[29], ~IN[30], ~IN[31]);  // And
  and and_4 (I[3], IN[29], IN[1], ~IN[2], ~IN[3], IN[4], IN[5], ~IN[6], ~IN[12], IN[13], IN[14], ~IN[25], ~IN[26], ~IN[27], ~IN[28], ~IN[29], ~IN[30], ~IN[31]);  // And
  and and_5 (I[4], IN[29], IN[1], ~IN[2], ~IN[3], IN[4], IN[5], ~IN[6], ~IN[12], ~IN[13], IN[14], ~IN[25], ~IN[26], ~IN[27], ~IN[28], ~IN[29], ~IN[30], ~IN[31]);  // And
  and and_6 (I[5], IN[29], IN[1], ~IN[2], ~IN[3], IN[4], ~IN[5], ~IN[6], ~IN[12], ~IN[13], ~IN[14]);  // And
  and and_7 (I[6], IN[29], IN[1], ~IN[2], ~IN[3], IN[4], ~IN[5], ~IN[6], IN[12], IN[13], IN[14]);  // And
  and and_8 (I[7], IN[29], IN[1], ~IN[2], ~IN[3], IN[4], ~IN[5], ~IN[6], ~IN[12], IN[13], IN[14]);  // And
  and and_9 (I[8], IN[29], IN[1], ~IN[2], ~IN[3], IN[4], ~IN[5], ~IN[6], ~IN[12], ~IN[13], IN[14]);  // And
  and and_10 (I[9], IN[29], IN[1], ~IN[2], ~IN[3], IN[4], IN[5], ~IN[6], ~IN[12], ~IN[13], ~IN[14], ~IN[25], ~IN[26], ~IN[27], ~IN[28], IN[29], ~IN[30], ~IN[31]);  // And
  and and_11 (I[10], IN[29], IN[1], ~IN[2], ~IN[3], IN[4], IN[5], ~IN[6], IN[12], ~IN[13], IN[14], ~IN[25], ~IN[26], ~IN[27], ~IN[28], ~IN[29], ~IN[30], ~IN[31]);  // And
  and and_12 (I[11], IN[29], IN[1], ~IN[2], ~IN[3], IN[4], IN[5], ~IN[6], IN[12], ~IN[13], IN[14], ~IN[25], ~IN[26], ~IN[27], ~IN[28], ~IN[29], IN[30], ~IN[31]);  // And
  and and_13 (I[12], IN[29], IN[1], ~IN[2], ~IN[3], IN[4], ~IN[5], ~IN[6], ~IN[12], ~IN[13], ~IN[14], ~IN[25], ~IN[26], ~IN[27], ~IN[28], IN[29], ~IN[30], ~IN[31]);  // And
  and and_14 (I[13], IN[29], IN[1], ~IN[2], ~IN[3], IN[4], ~IN[5], ~IN[6], IN[12], ~IN[13], IN[14], ~IN[25], ~IN[26], ~IN[27], ~IN[28], ~IN[29], ~IN[30], ~IN[31]);  // And
  and and_15 (I[14], IN[29], IN[1], ~IN[2], ~IN[3], IN[4], ~IN[5], ~IN[6], IN[12], ~IN[13], IN[14], ~IN[25], ~IN[26], ~IN[27], ~IN[28], ~IN[29], IN[30], ~IN[31]);  // And
  and and_16 (I[15], IN[29], IN[1], ~IN[2], ~IN[3], IN[4], IN[5], ~IN[6], ~IN[12], IN[13], ~IN[14], ~IN[25], ~IN[26], ~IN[27], ~IN[28], ~IN[29], ~IN[30], ~IN[31]);  // And
  and and_17 (I[16], IN[29], IN[1], ~IN[2], ~IN[3], IN[4], IN[5], ~IN[6], IN[12], IN[13], ~IN[14], ~IN[25], ~IN[26], ~IN[27], ~IN[28], ~IN[29], ~IN[30], ~IN[31]);  // And
  and and_18 (I[17], IN[29], IN[1], ~IN[2], ~IN[3], IN[4], ~IN[5], ~IN[6], ~IN[12], IN[13], ~IN[14]);  // And
  and and_19 (I[18], IN[29], IN[1], ~IN[2], ~IN[3], IN[4], ~IN[5], ~IN[6], IN[12], IN[13], ~IN[14]);  // And
  and and_20 (I[19], IN[29], IN[1], IN[2], ~IN[3], IN[4], IN[5], ~IN[6]);  // And
  and and_21 (I[20], IN[29], IN[1], IN[2], ~IN[3], IN[4], ~IN[5], ~IN[6]);  // And
  and and_22 (I[21], IN[29], IN[1], IN[2], IN[3], ~IN[4], IN[5], IN[6]);  // And
  and and_23 (I[22], IN[29], IN[1], IN[2], ~IN[3], ~IN[4], IN[5], IN[6], ~IN[12], ~IN[13], ~IN[14]);  // And
  and and_24 (I[23], IN[29], IN[1], ~IN[2], ~IN[3], ~IN[4], IN[5], IN[6], ~IN[12], ~IN[13], ~IN[14]);  // And
  and and_25 (I[24], IN[29], IN[1], ~IN[2], ~IN[3], ~IN[4], IN[5], IN[6], IN[12], ~IN[13], ~IN[14]);  // And
  and and_26 (I[25], IN[29], IN[1], ~IN[2], ~IN[3], ~IN[4], IN[5], IN[6], ~IN[12], ~IN[13], IN[14]);  // And
  and and_27 (I[26], IN[29], IN[1], ~IN[2], ~IN[3], ~IN[4], IN[5], IN[6], IN[12], ~IN[13], IN[14]);  // And
  and and_28 (I[27], IN[29], IN[1], ~IN[2], ~IN[3], ~IN[4], IN[5], IN[6], ~IN[12], IN[13], IN[14]);  // And
  and and_29 (I[28], IN[29], IN[1], ~IN[2], ~IN[3], ~IN[4], IN[5], IN[6], IN[12], IN[13], IN[14]);  // And
  and and_30 (I[29], IN[29], IN[1], ~IN[2], ~IN[3], ~IN[4], ~IN[5], ~IN[6], ~IN[12], ~IN[13], ~IN[14]);  // And
  and and_31 (I[30], IN[29], IN[1], ~IN[2], ~IN[3], ~IN[4], ~IN[5], ~IN[6], IN[12], ~IN[13], ~IN[14]);  // And
  and and_32 (I[31], IN[29], IN[1], ~IN[2], ~IN[3], ~IN[4], ~IN[5], ~IN[6], ~IN[12], IN[13], ~IN[14]);  // And
  and and_33 (I[32], IN[29], IN[1], ~IN[2], ~IN[3], ~IN[4], ~IN[5], ~IN[6], ~IN[12], ~IN[13], IN[14]);  // And
  and and_34 (I[33], IN[29], IN[1], ~IN[2], ~IN[3], ~IN[4], ~IN[5], ~IN[6], IN[12], ~IN[13], IN[14]);  // And
  and and_35 (I[34], IN[29], IN[1], ~IN[2], ~IN[3], ~IN[4], IN[5], ~IN[6], ~IN[12], ~IN[13], ~IN[14]);  // And
  and and_36 (I[35], IN[29], IN[1], ~IN[2], ~IN[3], ~IN[4], IN[5], ~IN[6], IN[12], ~IN[13], ~IN[14]);  // And
  and and_37 (I[36], IN[29], IN[1], ~IN[2], ~IN[3], ~IN[4], IN[5], ~IN[6], ~IN[12], IN[13], ~IN[14]);  // And
  nor nor_1 (R, I[0], I[1], I[2], I[3], I[4], I[5], I[6], I[7], I[8], I[9], I[10], I[11], I[12], I[13], I[14], I[15], I[16], I[17], I[18], I[19], I[20], I[21], I[22], I[23], I[24], I[25], I[26], I[27], I[28], I[29], I[30], I[31], I[32], I[33], I[34], I[35], I[36]);
  // Pins of 1 and 32 bits meet at {IN[31:1], IN[29]}

  assign IN[0] = IN[29];

  // Notes on the sheet:
  //   ADD
  //   SUB
  //   AND
  //   OR
  //   XOR
  //   ADDI
  //   ANDI
  //   ORI
  //   XORI
  //   SLL
  //   SRL
  //   SRA
  //   SLLI
  //   SRLI
  //   SRAI
  //   SLT
  //   SLTU
  //   SLTI
  //   SLTIU
  //   LUI
  //   AUIPC
  //   JAL
  //   JALR
  //   BEQ
  //   BNE
  //   BLT
  //   BGE
  //   BLTU
  //   BGEU
  //   LB
  //   LH
  //   LW
  //   LBU
  //   LHU
  //   SB
  //   SH
  //   SW
endmodule
