// Digital circuit RV32I.dig as structural Verilog
module RV32I (
  input  CLC
);

  wire and_1_out, BOOT, BOOT_CNT_EN, BOOT_CNT_ovf, BOOT_COMPLETE, BOOT_q, CLC_t, comparator_2_gt,
       EXECUTE_BRANCH_HOLD, GO, INSTR_DECODE_EN, INSTR_EXECUTE_EN, INSTR_MEMORY_EN, jk_ff_1_nq,
       MEMORY_BRANCH_HOLD, nand_1_out, nor_1_out, NORMAL, not_1_out, not_2_out, or_1_out, P_out, PC_EN,
       R_out, RESERVE, RESET, RUN_q, rv32i_instruction_decoder_2_p2, rv32i_register_reserve_1_hold, S_out;
  wire [1:0] CONTROL_FSM_out;
  wire [23:0] MEM_R_W_A, PC_IN, PC_INC_OUT, PC_OUT, ROM_A;
  wire [31:0] ALU_OUT, driver_5_out, driver_6_out, driver_7_out, driver_8_out, INSTR_DECODE, INSTR_EXECUTE,
       INSTR_MEMORY, INSTR_WRITE, MEM_R_W, RESULT_q, ROM, RS1, RS2;
  wire [31:24] driver_13_out;
  wire [36:0] rv32i_instruction_decoder_1_p2, rv32i_instruction_decoder_2_p3, rv32i_instruction_decoder_3_p2;

  nand nand_1 (nand_1_out, RESET, NORMAL);
  assign CLC_t = nand_1_out ? CLC : 1'bz;  // Driver driver_1
  Button S (.out(S_out));
  JK_FF jk_ff_1 (.J(S_out), .C(CLC_t), .K(~S_out), .nQ(jk_ff_1_nq));  // open: Q
  Button R (.out(R_out));
  and and_1 (and_1_out, S_out, jk_ff_1_nq);
  Button P (.out(P_out));
  LookUpTable #(.Bits(2)) CONTROL_FSM (
    .in0(BOOT), .in1(PC_EN), .in2(P_out), .in3(and_1_out), .in4(R_out), .out(CONTROL_FSM_out));
  D_FF RUN (.D(CONTROL_FSM_out[0]), .C(CLC_t), .Q(RUN_q));  // open: nQ
  D_FF #(.Default(1)) u_BOOT (.D(CONTROL_FSM_out[1]), .C(CLC_t), .Q(BOOT_q), .nQ(NORMAL));
  or or_1 (or_1_out, BOOT_COMPLETE, BOOT_CNT_ovf);
  and and_2 (PC_EN, ~or_1_out, RUN_q);  // And
  and and_3 (BOOT, BOOT_q, ~or_1_out);  // And
  and and_4 (BOOT_CNT_EN, BOOT, PC_EN);
  Seven_Seg_Hex seven_seg_hex_1 (.d(ROM[31:28]), .dp(1'b0));
  Counter #(.Bits(24)) BOOT_CNT (.en(BOOT_CNT_EN), .C(CLC_t), .clr(NORMAL), .out(ROM_A), .ovf(BOOT_CNT_ovf));
  Seven_Seg_Hex seven_seg_hex_2 (.d(ROM_A[23:20]), .dp(1'b0));
  Seven_Seg_Hex seven_seg_hex_3 (.d(ROM[27:24]), .dp(1'b0));
  Seven_Seg_Hex seven_seg_hex_4 (.d(ROM[23:20]), .dp(1'b0));
  ROM #(.AddrBits(24), .isProgramMemory("true"), .Bits(32)) u_ROM (.A(ROM_A), .sel(1'b1), .D(ROM));
  Comparator #(.Bits(24)) comparator_1 (.a(ROM_A), .b(24'h3c), .eq(BOOT_COMPLETE));  // open: gt, lt
  assign MEM_R_W_A = BOOT ? ROM_A : 24'bz;  // Driver driver_2
  Seven_Seg_Hex seven_seg_hex_5 (.d(ROM_A[19:16]), .dp(1'b0));
  Seven_Seg_Hex seven_seg_hex_6 (.d(ROM_A[15:12]), .dp(1'b0));
  Seven_Seg_Hex seven_seg_hex_7 (.d(ROM[19:16]), .dp(1'b0));
  Seven_Seg_Hex seven_seg_hex_8 (.d(ROM[15:12]), .dp(1'b0));
  Seven_Seg_Hex seven_seg_hex_9 (.d(ROM_A[11:8]), .dp(1'b0));
  Seven_Seg_Hex seven_seg_hex_10 (.d(ROM_A[7:4]), .dp(1'b0));
  Seven_Seg_Hex seven_seg_hex_11 (.d(ROM[11:8]), .dp(1'b0));
  Seven_Seg_Hex seven_seg_hex_12 (.d(ROM[7:4]), .dp(1'b0));
  Seven_Seg_Hex seven_seg_hex_13 (.d(ROM_A[3:0]), .dp(1'b0));
  Seven_Seg_Hex seven_seg_hex_14 (.d(ROM[3:0]), .dp(1'b0));
  Seven_Seg_Hex seven_seg_hex_15 (.d(MEM_R_W[31:28]), .dp(1'b0));
  Seven_Seg_Hex seven_seg_hex_16 (.d(MEM_R_W_A[23:20]), .dp(1'b0));
  Seven_Seg_Hex seven_seg_hex_17 (.d(MEM_R_W[27:24]), .dp(1'b0));
  Seven_Seg_Hex seven_seg_hex_18 (.d(MEM_R_W[23:20]), .dp(1'b0));
  Seven_Seg_Hex seven_seg_hex_19 (.d(MEM_R_W_A[19:16]), .dp(1'b0));
  Seven_Seg_Hex seven_seg_hex_20 (.d(MEM_R_W_A[15:12]), .dp(1'b0));
  Seven_Seg_Hex seven_seg_hex_21 (.d(MEM_R_W[19:16]), .dp(1'b0));
  Seven_Seg_Hex seven_seg_hex_22 (.d(MEM_R_W[15:12]), .dp(1'b0));
  Register #(.Bits(24), .isProgramCounter("true")) PC (.D(PC_IN), .C(CLC_t), .en(PC_EN), .Q(PC_OUT));
  Add #(.Bits(24)) PC_INC (.a(PC_OUT), .b(24'h1), .c_i(1'b0), .s(PC_INC_OUT));  // open: c_o
  PullDown #(.Bits(24)) pulldown_1 (.out(PC_IN));
  Seven_Seg_Hex seven_seg_hex_23 (.d(MEM_R_W_A[11:8]), .dp(1'b0));
  Seven_Seg_Hex seven_seg_hex_24 (.d(MEM_R_W_A[7:4]), .dp(1'b0));
  Seven_Seg_Hex seven_seg_hex_25 (.d(MEM_R_W[11:8]), .dp(1'b0));
  Seven_Seg_Hex seven_seg_hex_26 (.d(MEM_R_W[7:4]), .dp(1'b0));
  assign PC_IN = NORMAL ? PC_INC_OUT : 24'bz;  // Driver driver_3
  Seven_Seg_Hex seven_seg_hex_27 (.d(MEM_R_W_A[3:0]), .dp(1'b0));
  Seven_Seg_Hex seven_seg_hex_28 (.d(MEM_R_W[3:0]), .dp(1'b0));
  Seven_Seg_Hex seven_seg_hex_29 (.d(INSTR_DECODE[31:28]), .dp(1'b0));
  not not_1 (not_1_out, BOOT);
  PullDown #(.Bits(24)) pulldown_2 (.out(MEM_R_W_A));
  Seven_Seg_Hex seven_seg_hex_30 (.d(PC_OUT[23:20]), .dp(1'b0));
  Seven_Seg_Hex seven_seg_hex_31 (.d(INSTR_DECODE[27:24]), .dp(1'b0));
  Seven_Seg_Hex seven_seg_hex_32 (.d(INSTR_DECODE[23:20]), .dp(1'b0));
  RAMDualAccess #(.AddrBits(24), .Bits(32)) Memory (
    .str(BOOT), .C(CLC_t), .ld(not_1_out), .A1(MEM_R_W_A), .Din1(MEM_R_W), .A2(PC_OUT), .D1(MEM_R_W),
    .D2(INSTR_DECODE));
  // RV32I_Instruction_Decoder rv32i_instruction_decoder_1: pin names not known; wires that end beside it: INSTR_DECODE, rv32i_instruction_decoder_1_p2
  Seven_Seg_Hex seven_seg_hex_33 (.d(PC_OUT[19:16]), .dp(1'b0));
  Seven_Seg_Hex seven_seg_hex_34 (.d(PC_OUT[15:12]), .dp(1'b0));
  Seven_Seg_Hex seven_seg_hex_35 (.d(INSTR_DECODE[19:16]), .dp(1'b0));
  Seven_Seg_Hex seven_seg_hex_36 (.d(INSTR_DECODE[15:12]), .dp(1'b0));
  assign MEM_R_W = BOOT ? ROM : 32'bz;  // Driver driver_4
  Seven_Seg_Hex seven_seg_hex_37 (.d(PC_OUT[11:8]), .dp(1'b0));
  Seven_Seg_Hex seven_seg_hex_38 (.d(PC_OUT[7:4]), .dp(1'b0));
  Seven_Seg_Hex seven_seg_hex_39 (.d(INSTR_DECODE[11:8]), .dp(1'b0));
  Seven_Seg_Hex seven_seg_hex_40 (.d(INSTR_DECODE[7:4]), .dp(1'b0));
  nor nor_1 (nor_1_out, rv32i_instruction_decoder_1_p2[23], rv32i_instruction_decoder_1_p2[24], rv32i_instruction_decoder_1_p2[25], rv32i_instruction_decoder_1_p2[26], rv32i_instruction_decoder_1_p2[27], rv32i_instruction_decoder_1_p2[28], rv32i_instruction_decoder_1_p2[34], rv32i_instruction_decoder_1_p2[35], rv32i_instruction_decoder_1_p2[36]);
  Seven_Seg_Hex seven_seg_hex_41 (.d(PC_OUT[3:0]), .dp(1'b0));
  Seven_Seg_Hex seven_seg_hex_42 (.d(INSTR_DECODE[3:0]), .dp(1'b0));
  Seven_Seg_Hex seven_seg_hex_43 (.d(INSTR_EXECUTE[31:28]), .dp(1'b0));
  and and_5 (RESERVE, NORMAL, PC_EN, GO, nor_1_out);
  Seven_Seg_Hex seven_seg_hex_44 (.d(INSTR_EXECUTE[27:24]), .dp(1'b0));
  Seven_Seg_Hex seven_seg_hex_45 (.d(INSTR_EXECUTE[23:20]), .dp(1'b0));
  assign driver_5_out = RESERVE ? INSTR_DECODE : 32'bz;  // Driver driver_5
  Seven_Seg_Hex seven_seg_hex_46 (.d(INSTR_EXECUTE[19:16]), .dp(1'b0));
  Seven_Seg_Hex seven_seg_hex_47 (.d(INSTR_EXECUTE[15:12]), .dp(1'b0));
  assign driver_6_out = GO ? INSTR_DECODE : 32'bz;  // Driver driver_6
  PullDown #(.Bits(32)) pulldown_3 (.out(driver_6_out));
  PullDown #(.Bits(32)) pulldown_4 (.out(driver_5_out));
  not not_2 (not_2_out, PC_OUT[0]);
  and and_6 (INSTR_DECODE_EN, NORMAL, PC_EN);
  Seven_Seg_Hex seven_seg_hex_48 (.d(INSTR_EXECUTE[11:8]), .dp(1'b0));
  Seven_Seg_Hex seven_seg_hex_49 (.d(INSTR_EXECUTE[7:4]), .dp(1'b0));
  Register #(.Bits(32)) INSTR (.D(driver_6_out), .C(CLC_t), .en(INSTR_DECODE_EN), .Q(INSTR_EXECUTE));
  RV32I_Register_Reserve rv32i_register_reserve_1 (
    .INSTR(driver_5_out), .CLC(CLC_t), .RE(not_2_out), .RO(PC_OUT[0]), .HOLD(rv32i_register_reserve_1_hold));
  Seven_Seg_Hex seven_seg_hex_50 (.d(INSTR_EXECUTE[3:0]), .dp(1'b0));
  Seven_Seg_Hex seven_seg_hex_51 (.d(INSTR_MEMORY[31:28]), .dp(1'b0));
  nor nor_2 (GO, rv32i_register_reserve_1_hold, EXECUTE_BRANCH_HOLD, MEMORY_BRANCH_HOLD);
  Seven_Seg_Hex seven_seg_hex_52 (.d(INSTR_MEMORY[27:24]), .dp(1'b0));
  Seven_Seg_Hex seven_seg_hex_53 (.d(INSTR_MEMORY[23:20]), .dp(1'b0));
  Comparator #(.Bits(24)) comparator_2 (.a(PC_OUT), .b(24'ha), .gt(comparator_2_gt));  // open: eq, lt
  Seven_Seg_Hex seven_seg_hex_54 (.d(INSTR_MEMORY[19:16]), .dp(1'b0));
  Seven_Seg_Hex seven_seg_hex_55 (.d(INSTR_MEMORY[15:12]), .dp(1'b0));
  // RV32I_Instruction_Decoder rv32i_instruction_decoder_2: pin names not known; wires that end beside it: INSTR_EXECUTE, rv32i_instruction_decoder_2_p2, rv32i_instruction_decoder_2_p3
  Seven_Seg_Hex seven_seg_hex_56 (.d(INSTR_MEMORY[11:8]), .dp(1'b0));
  Seven_Seg_Hex seven_seg_hex_57 (.d(INSTR_MEMORY[7:4]), .dp(1'b0));
  and and_7 (RESET, comparator_2_gt, rv32i_instruction_decoder_2_p2);
  Seven_Seg_Hex seven_seg_hex_58 (.d(INSTR_MEMORY[3:0]), .dp(1'b0));
  Seven_Seg_Hex seven_seg_hex_59 (.d(INSTR_WRITE[31:28]), .dp(1'b0));
  assign driver_7_out = 1'b0 ? RS1 : 32'bz;  // Driver driver_7
  PullDown #(.Bits(32)) pulldown_5 (.out(driver_7_out));
  assign driver_8_out = 1'b0 ? RS1 : 32'bz;  // Driver driver_8
  PullDown #(.Bits(32)) pulldown_6 (.out(driver_8_out));
  or or_2 (EXECUTE_BRANCH_HOLD, rv32i_instruction_decoder_2_p3[21], rv32i_instruction_decoder_2_p3[22], rv32i_instruction_decoder_2_p3[23], rv32i_instruction_decoder_2_p3[24], rv32i_instruction_decoder_2_p3[25], rv32i_instruction_decoder_2_p3[26], rv32i_instruction_decoder_2_p3[27], rv32i_instruction_decoder_2_p3[28]);
  Seven_Seg_Hex seven_seg_hex_60 (.d(INSTR_WRITE[27:24]), .dp(1'b0));
  Seven_Seg_Hex seven_seg_hex_61 (.d(INSTR_WRITE[23:20]), .dp(1'b0));
  assign driver_7_out = 1'b0 ? RS2 : 32'bz;  // Driver driver_9
  assign driver_8_out = 1'b0 ? RS2 : 32'bz;  // Driver driver_10
  Seven_Seg_Hex seven_seg_hex_62 (.d(INSTR_WRITE[19:16]), .dp(1'b0));
  Seven_Seg_Hex seven_seg_hex_63 (.d(INSTR_WRITE[15:12]), .dp(1'b0));
  assign driver_7_out = 1'b0 ? MEM_R_W : 32'bz;  // Driver driver_11
  assign driver_8_out = 1'b0 ? {{8{1'b0}}, PC_OUT} : 32'bz;  // Driver driver_12
  Seven_Seg_Hex seven_seg_hex_64 (.d(INSTR_WRITE[11:8]), .dp(1'b0));
  Seven_Seg_Hex seven_seg_hex_65 (.d(INSTR_WRITE[7:4]), .dp(1'b0));
  Register #(.Bits(32)) INSTR_2 (.D(INSTR_EXECUTE), .C(CLC_t), .en(INSTR_EXECUTE_EN), .Q(INSTR_MEMORY));
  RV32I_ALU ALU (.A(driver_7_out), .B(driver_8_out), .Y(ALU_OUT), .O(4'b0001), .S({6{1'b0}}));  // open: SO
  Seven_Seg_Hex seven_seg_hex_66 (.d(INSTR_WRITE[3:0]), .dp(1'b0));
  and and_8 (INSTR_EXECUTE_EN, NORMAL, PC_EN);
  assign {driver_13_out, PC_IN} = 1'b0 ? ALU_OUT : 32'bz;  // Driver driver_13
  // RV32I_Instruction_Decoder rv32i_instruction_decoder_3: pin names not known; wires that end beside it: INSTR_MEMORY, rv32i_instruction_decoder_3_p2
  or or_3 (MEMORY_BRANCH_HOLD, rv32i_instruction_decoder_3_p2[21], rv32i_instruction_decoder_3_p2[22], rv32i_instruction_decoder_3_p2[23], rv32i_instruction_decoder_3_p2[24], rv32i_instruction_decoder_3_p2[25], rv32i_instruction_decoder_3_p2[26], rv32i_instruction_decoder_3_p2[27], rv32i_instruction_decoder_3_p2[28]);
  Register #(.Bits(32)) INSTR_3 (.D(INSTR_MEMORY), .C(CLC_t), .en(INSTR_MEMORY_EN), .Q(INSTR_WRITE));
  Register #(.Bits(32)) RESULT (.D(ALU_OUT), .C(CLC_t), .en(1'b0), .Q(RESULT_q));
  and and_9 (INSTR_MEMORY_EN, NORMAL, PC_EN);
  RegisterFile #(.AddrBits(5), .Bits(32)) registerfile_1 (
    .Din(RESULT_q), .we(1'b0), .Rw(INSTR_WRITE[11:7]), .C(CLC_t), .Ra({5{1'b0}}), .Rb({5{1'b0}}), .Da(RS1),
    .Db(RS2));

  // Other names for the same wires on the sheet: PC_INC_SET_PC = NORMAL; BOOT_CNT_SET_MEM_R_W_A = BOOT;
  //   MEM_STR = BOOT; ROM_SET_MEM_R_W = BOOT; RUN = PC_EN

  // Notes on the sheet:
  //   CLC: Hz: 20
  //   contents of CONTROL_FSM (hex, n*v repeats v):
  //   0,2,1,3,0,2,0,2,1,3,1,3,0,2,0,2,2,2,3,3,2,2,2,2,3,3,3,3,2,2,2,2
  //   contents of ROM (hex, n*v repeats v):
  //   280006f,aaaaaaaa,2,3,4,5,6,7,8,9,a,0,0,0,0,0,0,0,0,0,1437,497,80848533,809405b3,b57633,
  //   b566b3,b54733,1341793,c55813,c5d893,fff7c913,ffb97993,57ea13,8a1ab3,8a5b33,808a5bb3,
  //   17b2c33,16bacb3,17b3d33,16bbdb3,bae13,b2e93,bbf13,243f93,100103,4010123,6011123,104103,
  //   8010123,a011123,101103,c011123,e012123,105103,10011123,12012123,13,fffff06f
  //   ROM
  //   PROGRAM LENGTH
  //   MEM R/W
  //   INSTR
  //   EXECUTE
  //   MEMORY
  //   WRITE
endmodule
